# Fritzing sketch FSR (saved by Fritzing 0.9.3b)
breadboards: 1

parts:
  Part1 = Analog Digital MUX Breakout
  Part2 = Arduino Uno (Rev3) - ICSP
  J1 = Basic Force Sensing Resistor (FSR) [package=THT]
  J2 = Basic Force Sensing Resistor (FSR) [package=THT]
  Part3 = Analog Digital MUX Breakout

nets:
  N1: Part1.C0, J1.pin_0
  N2: Part1.C1, J2.pin_0
  GND: Part1.GND, Part1.S1, Part1.S2, Part1.S3, Part2.GND, Part3.GND, Part3.EN
  VCC: Part1.VCC, Part1.EN, Part2.5V, Part3.VCC, Part3.SIG
  N3: Part1.S0, Part2.D12/MISO
  N4: Part1.SIG, Part2.A1
  N5: Part2.D8, Part3.S0

// code stored in the sketch: FSR.ino
const int fsrPin = A0; // Analog pin connected to FSR

void setup() {
  Serial.begin(9600); // Initialize serial communication
  pinMode(0, OUTPUT);
  pinMode(1, OUTPUT);
  pinMode(2, OUTPUT);
  pinMode(3, OUTPUT);
  pinMode(8, OUTPUT);
  pinMode(9, OUTPUT);
  pinMode(10, OUTPUT);
  pinMode(11, OUTPUT);
}
void loop() {
  digitalWrite(0,LOW);
  int fsrValue = analogRead(fsrPin); // Read FSR value from analog pin
    Serial.println("Row 0:");
    for(int i=0;i<16;i++){
      Serial.println("Row" i":");
      for(int j=0;j<16;j++){
        //Varies of 8 and one other high
        digitalWrite(8,HIGH);
        Serial.print(fsrValue); //1
        digitalWrite(9,HIGH);
        Serial.print(fsrValue); //2
        digitalWrite(9,LOW);
        digitalWrite(10,HIGH);
        Serial.print(fsrValue); //3
        digitalWrite(10,LOW);
        digitalWrite(11,HIGH);
        Serial.print(fsrValue); //4
        digitalWrite(11,LOW);
        //Varies of 8 and 9 and one other high
        digitalWrite(9,HIGH);
        digitalWrite(10,HIGH);
        Serial.print(fsrValue); //5
        digitalWrite(10,LOW);
        digitalWrite(11,HIGH);
        Serial.print(fsrValue); //6
        digitalWrite(11,LOW);
        //Varies of 8 and 10 and one other up
        digitalWrite(10,HIGH);
        digitalWrite(9,LOW);
        digitalWrite(11,HIGH);
        Serial.print(fsrValue); //7
        digitalWrite(11,LOW);
        //Varies of 8 and 11 and 12 up
        digitalWrite(11,HIGH);
        Serial.print(fsrValue); //8
        //All on
        digitalWrite(8,HIGH);
        digitalWrite(9,HIGH);
        digitalWrite(10,HIGH);
        digitalWrite(11,HIGH);
        Serial.print(fsrValue); //9
        //All off
        digitalWrite(8,LOW);
        digitalWrite(9,LOW);
        digitalWrite(10,LOW);
        digitalWrite(11,LOW);
        Serial.print(fsrValue); //10
        // no 8 but solos
        digitalWrite(9,HIGH);
        Serial.print(fsrValue); //11
        digitalWrite(9,LOW);
        digitalWrite(10,HIGH);
        Serial.print(fsrValue); //12
        digitalWrite(10,LOW);
        digitalWrite(11,HIGH);
        Serial.print(fsrValue); //13
        digitalWrite(11,LOW);
        //just 9 and one other on
        digitalWrite(9,HIGH);
        digitalWrite(10,HIGH);
        Serial.print(fsrValue); //14
        digitalWrite(10,LOW);
        digitalWrite(11,HIGH);
        Serial.print(fsrValue); //15
        digitalWrite(9,LOW);
        //10 and 11 only
        digitalWrite(10,HIGH);
        digitalWrite(11,HIGH);
        Serial.print(fsrValue); //16
      }
    }
    Serial.println("FSR0:");
    Serial.print(fsrValue);
    Serial.println();
  delay(500);
  digitalWrite(12,LOW);
  Serial.println("FSR1:");
    Serial.print(fsrValue);
    Serial.println();
    delay(500);
  digitalWrite(8,LOW);
  Serial.println("FSR2:");
    Serial.print(fsrValue);
    Serial.println();
  delay(500);
  digitalWrite(12,HIGH);
  fsrValue = analogRead(fsrPin); // Read FSR value from analog pin
    Serial.println("FSR3:"); 
    Serial.print(fsrValue);
    Serial.println();
  delay(500);


}
